// Logisim project projeto.circ as structural Verilog: 9 circuits, main circuit projeto_main
module projeto_main (
);

  Multiplexer multiplexer_1 ();  // open: in0, in1, out, sel, en
  Multiplexer multiplexer_2 ();  // open: in0, in1, out, sel, en
endmodule

module meio_somador (
  input  A,
  input  B,
  output Soma,
  output CarryOut
);

  xor xor_1 (Soma, A, B);
  and and_1 (CarryOut, A, B);
endmodule

module meio_subtrator (
  input  A,
  input  B,
  output S,
  output Tout
);

  xor xor_1 (S, A, B);
  and and_1 (Tout, B, ~A);  // AND_Gate
endmodule

module multiplicacao (
  input  A1,
  input  A0,
  input  B1,
  input  B0,
  output P3,
  output P2,
  output P1,
  output P0
);

  wire and_1_out, and_2_out, and_3_out, meio_somador_2_carryout;

  and and_1 (and_1_out, A1, B1);
  meio_somador meio_somador_1 (.A(meio_somador_2_carryout), .B(and_1_out), .Soma(P2), .CarryOut(P3));
  and and_2 (and_2_out, A1, B0);
  meio_somador meio_somador_2 (.A(and_3_out), .B(and_2_out), .Soma(P1), .CarryOut(meio_somador_2_carryout));
  and and_3 (and_3_out, A0, B1);
  and and_4 (P0, A0, B0);
endmodule

module \and  (
  input  A,
  input  B,
  output S
);

  and and_1 (S, A, B);
endmodule

module \or  (
  input  A,
  input  B,
  output S
);

  or or_1 (S, A, B);
endmodule

module inversora (
  input  B,
  output S
);

  not not_1 (S, B);
endmodule

module ou_exclusivo (
  input  A,
  input  B,
  output S
);

  wire and_1_out, and_2_out, not_1_out, not_2_out;

  not not_1 (not_1_out, B);
  not not_2 (not_2_out, A);
  and and_1 (and_1_out, A, not_1_out);
  and and_2 (and_2_out, not_2_out, B);
  or or_1 (S, and_1_out, and_2_out);
endmodule

module deslocamento_esquerda (
  input  in_1,
  input  in_2,
  output out_3
);

  wire clock_1_out, d_ff_2_q, d_ff_3_q, d_ff_4_q;

  Clock clock_1 (.out(clock_1_out));
  D_Flip_Flop d_ff_1 (.clk(clock_1_out), .D(d_ff_2_q), .Q(out_3), .reset(in_2));  // open: Qn, preset, en
  D_Flip_Flop d_ff_2 (.clk(clock_1_out), .D(d_ff_3_q), .Q(d_ff_2_q), .reset(in_2));  // open: Qn, preset, en
  D_Flip_Flop d_ff_3 (.clk(clock_1_out), .D(d_ff_4_q), .Q(d_ff_3_q), .reset(in_2));  // open: Qn, preset, en
  D_Flip_Flop d_ff_4 (.clk(clock_1_out), .D(in_1), .Q(d_ff_4_q), .reset(in_2));  // open: Qn, preset, en
endmodule
